// Logisim project AktuellerStand.circ as structural Verilog: 2 circuits, main circuit main
module main (
  input  [4:0] in_1,
  input  Debug_ON,
  input  [1:0] PLAYER_JOYSTICK,
  input  SHOOT,
  input  RIGHT,
  output out_6
);

  wire ADD_OVERFLOW, ALU_CARRY_FLAG, alu_flag_status_1_out_10, ALU_IDB_B_SIGN_DIFFERENT, ALU_IDB_B_SIGN_SAME,
       ALU_IDB_RESULT_SIGN_DIFFERENT, ALU_OVERFLOW_FLAG, ALU_ZERO_FLAG, and_1_out, and_2_out, and_4_out,
       and_5_out, and_11_out, and_12_out, and_16_out, and_17_out, and_18_out, and_19_out, BG_SET, BRICK_HERE,
       BUSY_EN, carry_ad, carry_sub, clk, clock_1_out, CO_CLEAR, CO_IO_ENABLE, CO_WRITE_Y, comparator_1_eq,
       comparator_2_eq, comparator_3_eq, counter_2_carry, CU_3_REG_OP, CU_ALU_FLAG_en, CU_ALU_RESULT_en,
       CU_ALU_RESULT_SIGN, CU_const8_en, CU_const8_H_set, CU_CONST_10_TO_PC, CU_decode, CU_execute, CU_fetch,
       CU_IDB_TO_PC, CU_P_en, CU_PC_Write_en, CU_RAM_READ_ENABLE, CU_RAM_WRITE_ENABLE, CU_Reg_rw,
       CU_Select_ALU_Source_ACC_Const8, CU_write_back, CX_EN, CY_EN, decoder_2_out0, decoder_2_out1,
       decoder_2_out2, decoder_2_out3, decoder_3_out0, decoder_3_out1, decoder_3_out2, decoder_3_out3,
       decoder_4_out0, decoder_4_out1, decoder_4_out2, decoder_4_out3, decoder_4_out4, decoder_5_out0,
       decoder_5_out1, decoder_5_out2, decoder_5_out3, decoder_5_out4, decoder_6_out0, decoder_6_out1,
       decoder_6_out2, decoder_6_out3, decoder_6_out4, decoder_6_out5, decoder_6_out6, decoder_6_out7,
       decoder_10_out0, decoder_10_out1, decoder_10_out2, decoder_11_out0, decoder_11_out1, DIV_ZERO,
       IM_NEUEN_RECHTECK, IN_0, IN_1_t, IN_2, IN_3, IN_4, IN_5, IN_6, IN_7, IN_8, IN_9, IN_10, IN_11, IN_12,
       IN_13, IN_14, IN_15, IO_EN_REALTIME_CLK, IO_LED_WRITE, IO_READ_JOYSTICK, IO_RNG_READ,
       IO_SCOREBOARD_WRITE, KB_AVAIL, L_VOM_NEUEN, LAST_PIXEL, last_px, last_row, LEFT, MOVE_ACTIVE,
       MOVE_START, nand_1_out, NEU_ENDE, NEU_START, or_2_out, or_3_out, or_4_out, or_9_out, PAD_RD,
       PHASE_END, PLAYER_MOVE_ACTIVE, R_VOM_NEUEN, RF_RegR_en, RF_RegW_en, ROW_END, SEL_CX, SEL_CY,
       SKIP_PIXEL, SPLASH_BUSY, SPLASH_BUSY_RD, SPLASH_PHASE, SPLASH_START, SPLASH_START_N, SUB_OVERFLOW,
       tile_x_0, tile_x_1, tile_x_2, tile_x_3, tile_y_0, tile_y_1, tile_y_2, tile_y_3, UEBER_NEUEN,
       undriven_2, undriven_4, undriven_5, undriven_6, UNTER_NEUEN, Vorteiler_carry, X_LAST, Y_LAST,
       ZEICHENPHASE, ZEICHENPHASE_VOR;
  wire [0:0] keyboard_1_avail, undriven_3;
  wire [1:0] CC_cycle_counter_q, JOY_X_OLD, rgbled_3_p4, SPRITE_MEMORY_data;
  wire [2:0] comparator_10_eq, CU_ALU_CMD, CU_Reg_Read_Select, CU_Reg_Write_Select, multiplexer_14_out;
  wire [2:2] CU_REG_SELECT;
  wire [3:0] adder_5_out, multiplexer_28_out, multiplier_2_out, PC_program_counter_q, PC_program_counter_q_2,
       PC_program_counter_q_3, Player_Tile, Player_X, Player_Y, register_3_q, register_3_q_2, undriven_7;
  wire [5:0] CU_ALU_FLAGS, off_x, off_y;
  wire [5:5] register_2_q;
  wire [6:0] keyboard_1_data;
  wire [7:0] adder_2_out, adder_3_out, ALT_LINKS, ALT_OBEN, ALT_RECHTS, ALT_UNTEN, CU_Opcode, IDB_LOW,
       MALE_LINKS, MALE_OBEN, MALE_RECHTS, MALE_UNTEN, multiplexer_5_out, multiplexer_7_out,
       multiplexer_12_out, multiplexer_13_out, NEU_LINKS, NEU_OBEN, NEU_RECHTS, NEU_UNTEN, rgb_video_1_p4,
       rgb_video_1_p5, Shadow_Register_8_L_q, SPLASH_CX, SPLASH_CY, X_q, Y_q;
  wire [7:6] px_x, px_y;
  wire [9:0] CMD_CONST_10;
  wire [14:0] multiplexer_20_out;
  wire [15:0] ACC, adder_1_out, adder_4_out, ALU_B, ALU_SHL_OUT, ALU_SHR_OUT, bit_extender_1_out,
       bit_extender_2_out, bit_extender_3_out, bit_extender_4_out, bit_extender_5_out, BRICK_COLOR, COLOR_FG,
       Color_q, COLOR_SEL, COLOR_TABLE_data, divider_1_out, divider_1_rem, IDB, Instruction_bus, MAR,
       multiplexer_6_out, multiplexer_9_out, multiplexer_10_out, multiplexer_15_out, multiplexer_17_out,
       multiplexer_18_out, multiplexer_22_out, multiplexer_24_out, multiplexer_25_out, multiplexer_26_out,
       OUT_0, OUT_1, OUT_2, OUT_3, OUT_4, OUT_5, OUT_6_t, OUT_7, OUT_8, OUT_9, OUT_10, OUT_11, OUT_12,
       OUT_13, OUT_14, OUT_15, OUT_ALU_AND, OUT_ALU_DIV, OUT_ALU_DIV_ZERO_UNCHECKED, OUT_ALU_MUL, OUT_ALU_OR,
       PC_program_counter, Realtime_clock_q, register_1_q, register_6_q, register_7_q, register_8_q,
       register_9_q, register_10_q, register_11_q, register_24_q, register_29_q, rgb_video_1_p6, SCORE,
       Selected_Tile, SPLASH_BG, subtractor_1_out, TILE_STATUS, undriven;
  wire [15:3] Flag_Register_q;
  wire [15:8] register_3_q_3;
  wire [15:11] IW_Instruction_word_q;
  wire [15:12] PC_program_counter_q_4;
  wire [25:18] uP_memory_data;

  Decoder #(.select(2)) decoder_1 (
    .out0(CU_write_back), .out1(CU_fetch), .out2(CU_decode), .out3(CU_execute), .sel(CC_cycle_counter_q));  // open: en
  Register #(.width(16)) IW_Instruction_word (
    .D(Instruction_bus), .en(CU_fetch), .Q({IW_Instruction_word_q, CU_REG_SELECT[2], CMD_CONST_10}), .clk(clk));  // open: clr
  Register #(.width(16)) register_1 (.D(IDB), .en(IO_LED_WRITE), .Q(register_1_q), .clk(clk));  // open: clr
  Counter #(.max('hffff), .width(16)) Realtime_clock (
    .Q(Realtime_clock_q), .clk(Vorteiler_carry));  // open: load, D, count, carry, up, clr
  Counter #(.max('h3f), .width(6)) Vorteiler (.carry(Vorteiler_carry), .clk(clk));  // open: load, D, count, Q, up, clr
  Comparator #(.width(16)) comparator_1 (
    .a({PC_program_counter_q_4, PC_program_counter_q_3, PC_program_counter_q_2, PC_program_counter_q}),
    .b(16'h30), .eq(comparator_1_eq));  // open: gt, lt
  Hex_Digit_Display hex_digit_display_1 (.value(Realtime_clock_q[15:12]));  // open: dp
  assign IDB = IO_EN_REALTIME_CLK ? Realtime_clock_q : 16'bz;  // Controlled_Buffer controlled_buffer_1
  Adder #(.width(16)) adder_1 (
    .a({PC_program_counter_q_4, PC_program_counter_q_3, PC_program_counter_q_2, PC_program_counter_q}),
    .b(16'h1), .out(adder_1_out));  // open: cin, cout
  Clock clock_1 (.out(clock_1_out));
  // RGBLED rgbled_1: pin names not known; wires that end beside it: register_1_q[1], register_1_q[0], register_1_q[2]
  // RGBLED rgbled_2: pin names not known; wires that end beside it: register_1_q[4], register_1_q[3], register_1_q[5]
  // RGBLED rgbled_3: pin names not known; wires that end beside it: register_1_q[7], register_1_q[6], register_1_q[8], rgbled_3_p4
  // RGBLED rgbled_4: pin names not known; wires that end beside it: register_1_q[10], register_1_q[9], register_1_q[11]
  // RGBLED rgbled_5: pin names not known; wires that end beside it: register_1_q[13], register_1_q[12], register_1_q[14]
  Hex_Digit_Display hex_digit_display_2 (.value(Realtime_clock_q[11:8]));  // open: dp
  Hex_Digit_Display hex_digit_display_3 (.value(Realtime_clock_q[7:4]));  // open: dp
  Comparator #(.width(5)) comparator_2 (.a(CMD_CONST_10[7:3]), .b(5'b00010), .eq(comparator_2_eq));  // open: gt, lt
  Comparator #(.mode("unsigned"), .width(5)) comparator_3 (
    .a(CMD_CONST_10[7:3]), .b(5'b00011), .eq(comparator_3_eq));  // open: gt, lt
  Multiplexer #(.width(8)) multiplexer_1 (.in0(ALT_LINKS), .in1(NEU_LINKS), .out(MALE_LINKS), .sel(NEU_START));
  Multiplexer #(.width(8)) multiplexer_2 (.in0(ALT_RECHTS), .in1(NEU_RECHTS), .out(MALE_RECHTS), .sel(NEU_ENDE));
  Multiplexer #(.width(8)) multiplexer_3 (.in0(ALT_OBEN), .in1(NEU_OBEN), .out(MALE_OBEN), .sel(NEU_START));
  Multiplexer #(.width(8)) multiplexer_4 (.in0(ALT_UNTEN), .in1(NEU_UNTEN), .out(MALE_UNTEN), .sel(NEU_ENDE));
  Counter #(.max('h3), .width(2)) CC_cycle_counter (
    .Q(CC_cycle_counter_q), .clk(clk));  // open: load, D, count, carry, up, clr
  Multiplexer #(.width(8)) multiplexer_5 (
    .in0({IW_Instruction_word_q, CU_REG_SELECT[2], CMD_CONST_10[9:8]}),
    .in1({IW_Instruction_word_q, CU_REG_SELECT[2], CMD_CONST_10[9], 1'b0}), .out(multiplexer_5_out),
    .sel(IW_Instruction_word_q[14]));
  nand nand_1 (nand_1_out, comparator_1_eq, Debug_ON);
  Hex_Digit_Display hex_digit_display_4 (.value(Realtime_clock_q[3:0]));  // open: dp
  assign bit_extender_1_out = {{15{1'b0}}, SPLASH_BUSY};  // Bit_Extender bit_extender_1
  and and_1 (and_1_out, comparator_2_eq, CU_P_en);
  and and_2 (and_2_out, comparator_3_eq, CU_P_en);
  Multiplexer #(.width(16)) multiplexer_6 (.in0(adder_1_out), .in1(IDB), .out(multiplexer_6_out), .sel(CU_IDB_TO_PC));
  and and_3 (clk, nand_1_out, clock_1_out);
  LedBar #(.matrixcols(4)) Joystick_Debug (
    .led0(rgbled_3_p4[1]), .led1(rgbled_3_p4[0]), .led2(JOY_X_OLD[1]), .led3(JOY_X_OLD[0]));
  assign IDB = SPLASH_BUSY_RD ? bit_extender_1_out : 16'bz;  // Controlled_Buffer controlled_buffer_2
  Decoder #(.select(3)) decoder_2 (
    .out0(decoder_2_out0), .out1(decoder_2_out1), .out2(decoder_2_out2), .out3(decoder_2_out3),
    .out4(SPLASH_START_N), .out5(SPLASH_BUSY_RD), .out6(PAD_RD), .out7(BG_SET), .sel(CMD_CONST_10[2:0]),
    .en(and_1_out));
  Decoder #(.select(3)) decoder_3 (
    .out0(decoder_3_out0), .out1(decoder_3_out1), .out2(decoder_3_out2), .out3(decoder_3_out3),
    .out4(MOVE_START), .out5(CO_IO_ENABLE), .out6(CO_WRITE_Y), .out7(CO_CLEAR), .sel(CMD_CONST_10[2:0]),
    .en(and_2_out));
  Register #(.width(1)) register_2 (.D(alu_flag_status_1_out_10), .Q(register_2_q[5]), .clk(clk));  // open: en, clr
  Multiplexer #(.select(2), .width(8)) multiplexer_7 (
    .in1({IW_Instruction_word_q, CU_REG_SELECT[2], 2'b00}), .in2({IW_Instruction_word_q, 3'b000}),
    .in3({IW_Instruction_word_q, 3'b000}), .out(multiplexer_7_out), .sel(IW_Instruction_word_q[14:13]));  // open: in0
  and and_4 (and_4_out, CU_P_en, ~CMD_CONST_10[3], ~CMD_CONST_10[4], ~CMD_CONST_10[5], ~CMD_CONST_10[6], ~CMD_CONST_10[7]);  // AND_Gate
  Joystick #(.bits(2)) joystick_1 ();  // open: x, y
  assign IDB = IO_READ_JOYSTICK ? {{12{1'b0}}, rgbled_3_p4, JOY_X_OLD} : 16'bz;  // Controlled_Buffer controlled_buffer_3
  Hex_Digit_Display hex_digit_display_5 (.value(register_3_q_2));  // open: dp
  Register #(.width(16)) register_3 (
    .D(IDB), .en(IO_SCOREBOARD_WRITE), .Q({register_3_q_3, register_3_q_2, register_3_q}), .clk(clk));  // open: clr
  and and_5 (and_5_out, CU_P_en, CMD_CONST_10[3], ~CMD_CONST_10[4], ~CMD_CONST_10[5], ~CMD_CONST_10[6], ~CMD_CONST_10[7]);  // AND_Gate
  Comparator #(.mode("unsigned")) comparator_4 (.a(SPLASH_CX), .b(NEU_LINKS), .lt(L_VOM_NEUEN));  // open: gt, eq
  Comparator #(.mode("unsigned")) comparator_5 (.a(SPLASH_CX), .b(NEU_RECHTS), .gt(R_VOM_NEUEN));  // open: eq, lt
  Comparator #(.mode("unsigned")) comparator_6 (.a(SPLASH_CY), .b(NEU_OBEN), .lt(UEBER_NEUEN));  // open: gt, eq
  Comparator #(.mode("unsigned")) comparator_7 (.a(SPLASH_CY), .b(NEU_UNTEN), .gt(UNTER_NEUEN));  // open: eq, lt
  ROM #(.addrWidth(16), .dataWidth(32)) uP_memory (
    .addr({register_2_q[5], in_1, CU_Opcode, CC_cycle_counter_q}),
    .data({uP_memory_data, CU_3_REG_OP, CU_RAM_WRITE_ENABLE, CU_RAM_READ_ENABLE, CU_CONST_10_TO_PC, CU_ALU_FLAG_en, CU_P_en, CU_IDB_TO_PC, CU_Select_ALU_Source_ACC_Const8, CU_Reg_rw, RF_RegR_en, RF_RegW_en, CU_ALU_RESULT_en, CU_ALU_CMD, CU_const8_H_set, CU_const8_en, CU_PC_Write_en, CU_ALU_FLAGS}));
  Multiplexer #(.width(8)) multiplexer_8 (
    .in0(multiplexer_5_out), .in1(multiplexer_7_out), .out(CU_Opcode), .sel(IW_Instruction_word_q[15]));
  Multiplexer #(.width(16)) multiplexer_9 (
    .in0(multiplexer_6_out), .in1({{6{1'b0}}, CMD_CONST_10}), .out(multiplexer_9_out), .sel(CU_CONST_10_TO_PC));
  Decoder #(.select(3)) decoder_4 (
    .out0(decoder_4_out0), .out1(decoder_4_out1), .out2(decoder_4_out2), .out3(decoder_4_out3),
    .out4(decoder_4_out4), .out5(IO_EN_REALTIME_CLK), .out6(IO_READ_JOYSTICK), .out7(IO_LED_WRITE),
    .sel(CMD_CONST_10[2:0]), .en(and_4_out));
  Hex_Digit_Display hex_digit_display_6 (.value(register_3_q));  // open: dp
  Decoder #(.select(3)) decoder_5 (
    .out0(decoder_5_out0), .out1(decoder_5_out1), .out2(decoder_5_out2), .out3(decoder_5_out3),
    .out4(decoder_5_out4), .out5(IO_SCOREBOARD_WRITE), .out6(IO_RNG_READ), .sel(CMD_CONST_10[2:0]),
    .en(and_5_out));  // open: out7
  Multiplexer #(.width(16)) multiplexer_10 (.in0(SPLASH_BG), .in1(COLOR_FG), .out(multiplexer_10_out), .sel(NEU_ENDE));
  Register #(.width(16)) u_PC_program_counter (
    .D(multiplexer_9_out), .en(CU_PC_Write_en),
    .Q({PC_program_counter_q_4, PC_program_counter_q_3, PC_program_counter_q_2, PC_program_counter_q}),
    .clk(clk));  // open: clr
  Register u_NEU_LINKS (.D(IDB_LOW), .en(decoder_2_out0), .Q(NEU_LINKS), .clk(clk));  // open: clr
  Register u_NEU_OBEN (.D(IDB_LOW), .en(decoder_2_out1), .Q(NEU_OBEN), .clk(clk));  // open: clr
  Register u_NEU_RECHTS (.D(IDB_LOW), .en(decoder_2_out2), .Q(NEU_RECHTS), .clk(clk));  // open: clr
  Register u_NEU_UNTEN (.D(IDB_LOW), .en(decoder_2_out3), .Q(NEU_UNTEN), .clk(clk));  // open: clr
  Register #(.width(16)) u_SPLASH_BG (.D(IDB), .en(BG_SET), .Q(SPLASH_BG), .clk(clk));  // open: clr
  Register u_ALT_LINKS (.D(IDB_LOW), .en(decoder_3_out0), .Q(ALT_LINKS), .clk(clk));  // open: clr
  Register u_ALT_OBEN (.D(IDB_LOW), .en(decoder_3_out1), .Q(ALT_OBEN), .clk(clk));  // open: clr
  Register u_ALT_RECHTS (.D(IDB_LOW), .en(decoder_3_out2), .Q(ALT_RECHTS), .clk(clk));  // open: clr
  Register u_ALT_UNTEN (.D(IDB_LOW), .en(decoder_3_out3), .Q(ALT_UNTEN), .clk(clk));  // open: clr
  // Probe on decoder_5_out4
  nor nor_1 (IM_NEUEN_RECHTECK, L_VOM_NEUEN, R_VOM_NEUEN, UEBER_NEUEN, UNTER_NEUEN);
  and and_6 (SKIP_PIXEL, IM_NEUEN_RECHTECK, ~SPLASH_PHASE, MOVE_ACTIVE);  // AND_Gate
  Multiplexer #(.width(16)) multiplexer_11 (
    .in0(multiplexer_10_out), .in1(BRICK_COLOR), .out(COLOR_SEL), .sel(BRICK_HERE));
  ALU_FLAG_STATUS alu_flag_status_1 (
    .ALU_Zero_Flag(ALU_ZERO_FLAG), .Bit0(CU_ALU_FLAGS[0]), .ALU_CARRY_Flag(ALU_CARRY_FLAG),
    .Bit1(CU_ALU_FLAGS[1]), .ALU_Overflow_Flag(ALU_OVERFLOW_FLAG), .Bit2(CU_ALU_FLAGS[2]),
    .Bit3(CU_ALU_FLAGS[3]), .Bit4(CU_ALU_FLAGS[4]), .Bit5(CU_ALU_FLAGS[5]), .out_10(alu_flag_status_1_out_10));
  Hex_Digit_Display hex_digit_display_7 (.value(PC_program_counter_q_3));  // open: dp
  Hex_Digit_Display hex_digit_display_8 (.value(PC_program_counter_q_4));  // open: dp
  TTY tty_1 (.data(IDB[6:0]), .clk(clk), .we(decoder_4_out0), .clr(decoder_4_out1));
  Keyboard keyboard_1 (
    .clk(clk), .re(decoder_4_out2), .clr(decoder_4_out3), .avail(keyboard_1_avail[0]), .data(keyboard_1_data));
  // Probe on X_q
  Register X (.D(IDB[7:0]), .en(decoder_5_out2), .Q(X_q), .clk(clk));  // open: clr
  // Probe on decoder_5_out2
  // Probe on Y_q
  Register Y (.D(IDB[7:0]), .en(decoder_5_out3), .Q(Y_q), .clk(clk));  // open: clr
  // Probe on decoder_5_out3
  // Probe on Color_q
  Register #(.width(16)) Color (.D(IDB), .en(decoder_5_out4), .Q(Color_q), .clk(clk));  // open: clr
  ROM #(.addrWidth(16), .dataWidth(16)) instruction_memory (
    .addr({PC_program_counter_q_4, PC_program_counter_q_3, PC_program_counter_q_2, PC_program_counter_q}),
    .data(Instruction_bus));
  Hex_Digit_Display hex_digit_display_9 (.value(PC_program_counter_q_2));  // open: dp
  Hex_Digit_Display hex_digit_display_10 (.value(PC_program_counter_q));  // open: dp
  assign IDB = decoder_4_out4 ? {{15{1'b0}}, keyboard_1_avail[0]} : 16'bz;  // Controlled_Buffer controlled_buffer_4
  // Random #(.width(16)) Randomgenerator: pin names not known; wires that end beside it: 1'b1, clk
  assign IDB = decoder_4_out2 ? {{9{1'b0}}, keyboard_1_data} : 16'bz;  // Controlled_Buffer controlled_buffer_5
  assign IDB = IO_RNG_READ ? undriven : 16'bz;  // Controlled_Buffer controlled_buffer_6
  Adder adder_2 (.a(SPLASH_CX), .b(8'h1), .out(adder_2_out), .cin(1'b0));  // open: cout
  Adder adder_3 (.a(SPLASH_CY), .b(8'h1), .out(adder_3_out), .cin(1'b0));  // open: cout
  or or_1 (ZEICHENPHASE, MOVE_START, SPLASH_PHASE);
  and and_7 (ZEICHENPHASE_VOR, ZEICHENPHASE, ~PHASE_END);  // AND_Gate
  or or_2 (or_2_out, SPLASH_START, SPLASH_PHASE);
  or or_3 (or_3_out, MOVE_START, LAST_PIXEL);
  or or_4 (or_4_out, MOVE_START, SPLASH_PHASE);
  or or_5 (SPLASH_START, SPLASH_START_N, MOVE_START);
  and and_8 (ROW_END, SPLASH_BUSY, X_LAST);
  Multiplexer #(.width(8)) multiplexer_12 (.in0(adder_2_out), .in1(MALE_LINKS), .out(multiplexer_12_out), .sel(SEL_CX));
  Multiplexer #(.width(8)) multiplexer_13 (.in0(adder_3_out), .in1(MALE_OBEN), .out(multiplexer_13_out), .sel(SEL_CY));
  Register #(.width(1)) u_SPLASH_BUSY (.D(or_2_out), .en(BUSY_EN), .Q(SPLASH_BUSY), .clk(clk));  // open: clr
  Register #(.width(1)) u_SPLASH_PHASE (.D(MOVE_START), .en(or_3_out), .Q(SPLASH_PHASE), .clk(clk));  // open: clr
  Register #(.width(1)) u_MOVE_ACTIVE (.D(or_4_out), .en(BUSY_EN), .Q(MOVE_ACTIVE), .clk(clk));  // open: clr
  Register u_SPLASH_CX (.D(multiplexer_12_out), .en(CX_EN), .Q(SPLASH_CX), .clk(clk));  // open: clr
  Register u_SPLASH_CY (.D(multiplexer_13_out), .en(CY_EN), .Q(SPLASH_CY), .clk(clk));  // open: clr
  or or_6 (BUSY_EN, SPLASH_START, LAST_PIXEL);
  and and_9 (PHASE_END, LAST_PIXEL, SPLASH_PHASE);
  and and_10 (LAST_PIXEL, SPLASH_BUSY, X_LAST, Y_LAST);
  or or_7 (NEU_START, ZEICHENPHASE_VOR, ~MOVE_ACTIVE);  // OR_Gate
  or or_8 (NEU_ENDE, ZEICHENPHASE, ~MOVE_ACTIVE);  // OR_Gate
  Register Shadow_Register_8_L (.D(IDB[7:0]), .Q(Shadow_Register_8_L_q), .clr(clk));  // open: en, clk
  Multiplexer #(.width(3)) multiplexer_14 (
    .in0(CU_Reg_Write_Select), .in1(CMD_CONST_10[8:6]), .out(multiplexer_14_out), .sel(CU_3_REG_OP));
  Demultiplexer #(.width(3)) demultiplexer_1 (
    .out0(CU_Reg_Read_Select), .out1(CU_Reg_Write_Select), .in({CU_REG_SELECT[2], CMD_CONST_10[9:8]}),
    .sel(CU_Reg_rw));
  or or_9 (or_9_out, undriven_2, KB_AVAIL);
  or or_10 (SEL_CX, SPLASH_START, X_LAST);
  or or_11 (CX_EN, SPLASH_START, SPLASH_BUSY);
  Comparator comparator_8 (.a(SPLASH_CX), .b(MALE_RECHTS), .eq(X_LAST));  // open: gt, lt
  Comparator comparator_9 (.a(SPLASH_CY), .b(MALE_UNTEN), .eq(Y_LAST));  // open: gt, lt
  assign IDB = CU_const8_en ? multiplexer_15_out : 16'bz;  // Controlled_Buffer controlled_buffer_7
  Multiplexer #(.width(16)) multiplexer_15 (
    .in0({{8{1'b0}}, CMD_CONST_10[7:0]}), .in1({CMD_CONST_10[7:0], Shadow_Register_8_L_q}),
    .out(multiplexer_15_out), .sel(CU_const8_H_set));
  Decoder #(.select(3)) decoder_6 (
    .out0(decoder_6_out0), .out1(decoder_6_out1), .out2(decoder_6_out2), .out3(decoder_6_out3),
    .out4(decoder_6_out4), .out5(decoder_6_out5), .out6(decoder_6_out6), .out7(decoder_6_out7),
    .sel(multiplexer_14_out), .en(RF_RegW_en));
  assign IDB = undriven_4 ? {{15{1'b0}}, undriven_3[0]} : 16'bz;  // Controlled_Buffer controlled_buffer_8
  or or_12 (SEL_CY, SPLASH_START, PHASE_END);
  or or_13 (CY_EN, SPLASH_START, ROW_END);
  Register #(.width(16)) register_4 (.D(IDB), .en(decoder_6_out0), .Q(ACC), .clk(clk));  // open: clr
  Register #(.width(16)) register_5 (.D(IDB), .en(decoder_6_out1), .Q(MAR), .clk(clk));  // open: clr
  Register #(.width(16)) register_6 (.D(IDB), .en(decoder_6_out2), .Q(register_6_q), .clk(clk));  // open: clr
  Register #(.width(16)) register_7 (.D(IDB), .en(decoder_6_out3), .Q(register_7_q), .clk(clk));  // open: clr
  Register #(.width(16)) register_8 (.D(IDB), .en(decoder_6_out4), .Q(register_8_q), .clk(clk));  // open: clr
  Register #(.width(16)) register_9 (.D(IDB), .en(decoder_6_out5), .Q(register_9_q), .clk(clk));  // open: clr
  Register #(.width(16)) register_10 (.D(IDB), .en(decoder_6_out6), .Q(register_10_q), .clk(clk));  // open: clr
  Register #(.width(16)) register_11 (.D(IDB), .en(decoder_6_out7), .Q(register_11_q), .clk(clk));  // open: clr
  Divider #(.width(16)) divider_1 (
    .a(SCORE), .b(16'h3e8), .out(divider_1_out), .upper({16{1'b0}}), .rem(divider_1_rem));
  and and_11 (and_11_out, CU_P_en, CMD_CONST_10[4], CMD_CONST_10[5], CMD_CONST_10[6], CMD_CONST_10[7]);
  xor xor_1 (ALU_IDB_B_SIGN_DIFFERENT, IDB[15], ALU_B[15]);
  xor xor_2 (ALU_IDB_RESULT_SIGN_DIFFERENT, IDB[15], CU_ALU_RESULT_SIGN);
  Decoder #(.select(4)) decoder_7 (
    .out0(IN_0), .out1(IN_1_t), .out2(IN_2), .out3(IN_3), .out4(IN_4), .out5(IN_5), .out6(IN_6), .out7(IN_7),
    .out8(IN_8), .out9(IN_9), .out10(IN_10), .out11(IN_11), .out12(IN_12), .out13(IN_13), .out14(IN_14),
    .out15(IN_15), .en(and_12_out));  // open: sel
  buf and_12 (and_12_out, and_11_out);  // AND_Gate
  Multiplexer #(.width(16)) multiplexer_16 (
    .in0(ACC), .in1({{8{1'b0}}, CMD_CONST_10[7:0]}), .out(ALU_B), .sel(CU_Select_ALU_Source_ACC_Const8));
  and and_13 (SUB_OVERFLOW, ALU_IDB_B_SIGN_DIFFERENT, ALU_IDB_RESULT_SIGN_DIFFERENT);
  Multiplexer #(.select(3), .width(16)) multiplexer_17 (
    .in0(ACC), .in1(MAR), .in2(register_6_q), .in3(register_7_q), .in4(register_8_q), .in5(register_9_q),
    .in6(register_10_q), .in7(register_11_q), .out(multiplexer_17_out), .sel(CU_Reg_Read_Select));
  Multiplexer #(.select(3), .width(16)) multiplexer_18 (
    .in0(ACC), .in1(MAR), .in2(register_6_q), .in3(register_7_q), .in4(register_8_q), .in5(register_9_q),
    .in6(register_10_q), .in7(register_11_q), .out(multiplexer_18_out), .sel(CMD_CONST_10[2:0]));
  not not_1 (ALU_IDB_B_SIGN_SAME, ALU_IDB_B_SIGN_DIFFERENT);
  and and_14 (ADD_OVERFLOW, ALU_IDB_B_SIGN_SAME, ALU_IDB_RESULT_SIGN_DIFFERENT);
  assign IDB = RF_RegR_en ? multiplexer_17_out : 16'bz;  // Controlled_Buffer controlled_buffer_9
  Subtractor #(.width(16)) subtractor_1 (.a(IDB), .b(ALU_B), .out(subtractor_1_out), .bin(1'b0), .bout(carry_sub));
  Adder #(.width(16)) adder_4 (.a(ALU_B), .b(IDB), .out(adder_4_out), .cin(1'b0), .cout(carry_ad));
  Register #(.width(16)) register_12 (.D(16'h2), .en(IN_0), .Q(OUT_0), .clk(clk));  // open: clr
  Register #(.width(16)) register_13 (.D(16'h3), .en(IN_4), .Q(OUT_4), .clk(clk));  // open: clr
  Register #(.width(16)) register_14 (.D({16{1'b0}}), .en(IN_8), .Q(OUT_8), .clk(clk));  // open: clr
  Register #(.width(16)) register_15 (.D({16{1'b0}}), .en(IN_12), .Q(OUT_12), .clk(clk));  // open: clr
  Hex_Digit_Display hex_digit_display_11 (.value(PC_program_counter[15:12]));  // open: dp
  // Probe on CU_fetch
  // Probe on CU_decode
  // Probe on CU_execute
  // Probe on CU_write_back
  RAM #(.addrWidth(16), .dataWidth(16)) ram_1 (
    .addr(multiplexer_18_out), .we(CU_RAM_WRITE_ENABLE), .oe(CU_RAM_READ_ENABLE), .clk(clk), .din(IDB),
    .dout(IDB));
  Multiplexer #(.select(3)) multiplexer_19 (
    .in0(carry_ad), .in1(carry_sub), .in2(1'b0), .in3(1'b0), .in4(1'b0), .in5(1'b0), .in6(1'b0), .in7(1'b0),
    .out(comparator_10_eq[1]), .sel(CU_ALU_CMD));
  Hex_Digit_Display hex_digit_display_12 (.value(PC_program_counter[11:8]));  // open: dp
  Register #(.width(16)) register_16 (.D(16'h3), .en(IN_1_t), .Q(OUT_1), .clk(clk));  // open: clr
  Register #(.width(16)) register_17 (.D(16'h2), .en(IN_5), .Q(OUT_5), .clk(clk));  // open: clr
  Register #(.width(16)) register_18 (.D({16{1'b0}}), .en(IN_9), .Q(OUT_9), .clk(clk));  // open: clr
  Register #(.width(16)) register_19 (.D(16'h1), .en(IN_13), .Q(OUT_13), .clk(clk));  // open: clr
  Hex_Digit_Display hex_digit_display_13 (.value(PC_program_counter[7:4]));  // open: dp
  Hex_Digit_Display hex_digit_display_14 (.value(PC_program_counter[3:0]));  // open: dp
  Multiplexer #(.select(3), .width(16)) multiplexer_20 (
    .in0(adder_4_out), .in1(subtractor_1_out), .in2(OUT_ALU_AND), .in3(OUT_ALU_OR), .in4(OUT_ALU_MUL),
    .in5(OUT_ALU_DIV), .in6(ALU_SHL_OUT), .in7(ALU_SHR_OUT), .out({CU_ALU_RESULT_SIGN, multiplexer_20_out}),
    .sel(CU_ALU_CMD));
  Multiplexer #(.select(3)) multiplexer_21 (
    .in0(ADD_OVERFLOW), .in1(SUB_OVERFLOW), .in2(1'b0), .in3(1'b0), .in4(1'b0), .in5(1'b0), .in6(1'b0),
    .in7(1'b0), .out(comparator_10_eq[2]), .sel(CU_ALU_CMD));
  Register #(.width(16)) register_20 (.D(16'h2), .en(IN_2), .Q(OUT_2), .clk(clk));  // open: clr
  Register #(.width(16)) register_21 (.D(16'h3), .en(IN_6), .Q(OUT_6_t), .clk(clk));  // open: clr
  Register #(.width(16)) register_22 (.D(16'h4), .en(IN_10), .Q(OUT_10), .clk(clk));  // open: clr
  Register #(.width(16)) register_23 (.D({16{1'b0}}), .en(IN_14), .Q(OUT_14), .clk(clk));  // open: clr
  Register #(.width(16)) register_24 (
    .D({CU_ALU_RESULT_SIGN, multiplexer_20_out}), .Q(register_24_q), .clk(clk));  // open: en, clr
  Comparator #(.width(16)) comparator_10 (
    .a({CU_ALU_RESULT_SIGN, multiplexer_20_out}), .b({16{1'b0}}), .eq(comparator_10_eq[0]));  // open: gt, lt
  Register #(.width(16)) register_25 (.D(16'h3), .en(IN_3), .Q(OUT_3), .clk(clk));  // open: clr
  Register #(.width(16)) register_26 (.D(16'h2), .en(IN_7), .Q(OUT_7), .clk(clk));  // open: clr
  Register #(.width(16)) register_27 (.D({16{1'b0}}), .en(IN_11), .Q(OUT_11), .clk(clk));  // open: clr
  Register #(.width(16)) register_28 (.D({16{1'b0}}), .en(IN_15), .Q(OUT_15), .clk(clk));  // open: clr
  assign IDB = CU_ALU_RESULT_en ? register_24_q : 16'bz;  // Controlled_Buffer controlled_buffer_10
  Comparator #(.width(16)) comparator_11 (.a(ALU_B), .b({16{1'b0}}), .eq(DIV_ZERO));  // open: gt, lt
  Multiplexer #(.width(16)) multiplexer_22 (.in0(ALU_B), .in1(16'h1), .out(multiplexer_22_out), .sel(DIV_ZERO));
  Register #(.width(16)) Flag_Register (
    .D({{13{1'b0}}, comparator_10_eq}), .en(CU_ALU_FLAG_en),
    .Q({Flag_Register_q, ALU_OVERFLOW_FLAG, ALU_CARRY_FLAG, ALU_ZERO_FLAG}), .clk(clk));  // open: clr
  assign OUT_ALU_AND = ALU_B & IDB;  // AND_Gate and_15, 16 bits wide
  Shifter #(.width(16)) shifter_1 (.in(IDB), .\dist (ALU_B[3:0]), .out(ALU_SHL_OUT));
  Shifter #(.shift("lr"), .width(16)) shifter_2 (.in(IDB), .\dist (ALU_B[3:0]), .out(ALU_SHR_OUT));
  assign OUT_ALU_OR = ALU_B | IDB;  // OR_Gate or_14, 16 bits wide
  Multiplier #(.width(16)) multiplier_1 (.a(ALU_B), .b(IDB), .out(OUT_ALU_MUL), .cin({16{1'b0}}));  // open: cout
  Divider #(.width(16)) divider_2 (
    .a(IDB), .b(multiplexer_22_out), .out(OUT_ALU_DIV_ZERO_UNCHECKED), .upper({16{1'b0}}));  // open: rem
  Multiplexer #(.width(16)) multiplexer_23 (
    .in0(OUT_ALU_DIV_ZERO_UNCHECKED), .in1({16{1'b0}}), .out(OUT_ALU_DIV), .sel(DIV_ZERO));
  Counter #(.max('h3), .width(2)) counter_1 (.Q(px_y), .clk(tile_x_0));  // open: load, D, count, carry, up, clr
  Counter #(.max('h3), .trigger("falling"), .width(2)) counter_2 (
    .Q(px_x), .carry(counter_2_carry), .clk(and_16_out));  // open: load, D, count, up, clr
  and and_16 (and_16_out, last_row, last_px);
  Counter #(.max('h3f), .trigger("falling"), .width(6)) counter_3 (
    .Q(off_y), .carry(last_row), .clk(last_px));  // open: load, D, count, up, clr
  Counter #(.max('h3f), .width(6)) counter_4 (.Q(off_x), .carry(last_px), .clk(clk));  // open: load, D, count, up, clr
  Decoder #(.select(2)) decoder_8 (
    .out0(tile_y_0), .out1(tile_y_1), .out2(tile_y_2), .out3(tile_y_3), .sel(px_y));  // open: en
  // Probe on px_y
  Decoder #(.select(2)) decoder_9 (
    .out0(tile_x_0), .out1(tile_x_1), .out2(tile_x_2), .out3(tile_x_3), .sel(px_x));  // open: en
  // Probe on px_x
  Random #(.width(4)) random_1 (.next(undriven_5), .clr(undriven_6));  // open: clk, out
  // Probe on off_y
  // Probe on off_x
  Controlled_Buffer #(.width(16)) controlled_buffer_11 (.in({{12{1'b0}}, undriven_7}), .out(IDB));  // open: en
  ROM #(.addrWidth(20), .dataWidth(2)) SPRITE_MEMORY (
    .addr({register_29_q[7:0], off_y, off_x}), .data(SPRITE_MEMORY_data));
  Register #(.trigger("falling"), .width(16)) register_29 (
    .D(Selected_Tile), .en(1'b1), .Q(register_29_q), .clk(and_16_out));  // open: clr
  Multiplexer #(.select(4), .width(16)) multiplexer_24 (
    .in0(OUT_0), .in1(OUT_1), .in2(OUT_2), .in3(OUT_3), .in4(OUT_4), .in5(OUT_5), .in6(OUT_6_t), .in7(OUT_7),
    .in8(OUT_8), .in9(OUT_9), .in10(OUT_10), .in11(OUT_11), .in12(OUT_12), .in13(OUT_13), .in14(OUT_14),
    .in15(OUT_15), .out(multiplexer_24_out), .sel(CMD_CONST_10[3:0]));
  and and_17 (and_17_out, CU_P_en, ~CMD_CONST_10[4], CMD_CONST_10[5], ~CMD_CONST_10[6], ~CMD_CONST_10[7]);  // AND_Gate
  assign IDB = and_17_out ? multiplexer_24_out : 16'bz;  // Controlled_Buffer controlled_buffer_12
  or or_15 (PLAYER_MOVE_ACTIVE, LEFT, RIGHT);
  ROM #(.addrWidth(2), .dataWidth(16)) COLOR_TABLE (.addr(SPRITE_MEMORY_data), .data(COLOR_TABLE_data));
  and and_18 (and_18_out, CU_P_en, ~CMD_CONST_10[4], ~CMD_CONST_10[5], ~CMD_CONST_10[6], CMD_CONST_10[7]);  // AND_Gate
  Decoder #(.select(2)) decoder_10 (
    .out0(decoder_10_out0), .out1(decoder_10_out1), .out2(decoder_10_out2), .out3(decoder_10_out2),
    .sel(PLAYER_JOYSTICK));  // open: en
  // RGB_Video #(.height(256), .width(256)) rgb_video_1: pin names not known; wires that end beside it: register_29_q, clk, 1'b1, rgb_video_1_p4, rgb_video_1_p5, rgb_video_1_p6
  // Probe on {2'b00, IDB[1:0]}
  Decoder #(.select(4)) decoder_11 (
    .out0(decoder_11_out0), .out1(decoder_11_out1), .sel(CMD_CONST_10[3:0]), .en(and_18_out));  // open: out2, out3, out4, out5, out6, out7, out8, out9, out10, out11, out12, out13, out14, out15
  Multiplexer #(.width(16)) multiplexer_25 (.in0(16'h2), .in1({16{1'b0}}), .out(multiplexer_25_out), .sel(SHOOT));
  Multiplexer #(.width(16)) multiplexer_26 (.in0({16{1'b0}}), .in1(16'h4), .out(multiplexer_26_out), .sel(SHOOT));
  assign bit_extender_2_out = {{15{1'b0}}, decoder_10_out0};  // Bit_Extender bit_extender_2
  assign bit_extender_3_out = {{15{1'b0}}, decoder_10_out1};  // Bit_Extender bit_extender_3
  assign bit_extender_4_out = {{15{1'b0}}, decoder_10_out2};  // Bit_Extender bit_extender_4
  assign bit_extender_5_out = {{15{1'b0}}, decoder_10_out2};  // Bit_Extender bit_extender_5
  // Probe on {2'b00, IDB[1:0]}
  Register #(.width(4)) u_Player_X (.D({2'b00, IDB[1:0]}), .en(decoder_11_out0), .Q(Player_X), .clk(clk));  // open: clr
  Register #(.width(4)) u_Player_Y (.D({2'b00, IDB[1:0]}), .en(decoder_11_out1), .Q(Player_Y), .clk(clk));  // open: clr
  Multiplexer #(.select(4), .width(16)) multiplexer_27 (
    .in0(16'h2), .in1(16'h3), .in2(multiplexer_25_out), .in3(16'h3), .in4(16'h3), .in5(16'h2), .in6(16'h3),
    .in7(16'h2), .in8({16{1'b0}}), .in9({16{1'b0}}), .in10(multiplexer_26_out), .in11({16{1'b0}}),
    .in12(bit_extender_2_out), .in13(bit_extender_3_out), .in14(bit_extender_4_out),
    .in15(bit_extender_5_out), .out(Selected_Tile), .sel({px_y, px_x}));
  Register register_30 (.D({px_x, off_x}), .Q(rgb_video_1_p4), .clk(clk));  // open: en, clr
  Register register_31 (.D({px_y, off_y}), .Q(rgb_video_1_p5), .clk(clk));  // open: en, clr
  Register #(.width(16)) register_32 (.D(COLOR_TABLE_data), .Q(rgb_video_1_p6), .clk(clk));  // open: en, clr
  Clock clock_2 ();  // open: out
  // Probe on 4'b0100
  // Probe on Player_Y
  // Probe on Player_X
  Multiplier #(.width(4)) multiplier_2 (.a(Player_Y), .b(4'b0100), .out(multiplier_2_out));  // open: cin, cout
  // Probe on multiplier_2_out
  Multiplexer #(.select(4), .width(4)) multiplexer_28 (
    .in0(Player_X), .in1(Player_Y), .in2(Player_Tile), .in3(TILE_STATUS[3:0]), .out(multiplexer_28_out),
    .sel(CMD_CONST_10[3:0]));  // open: in4, in5, in6, in7, in8, in9, in10, in11, in12, in13, in14, in15
  Adder #(.width(4)) adder_5 (.a(Player_X), .b(multiplier_2_out), .out(adder_5_out));  // open: cin, cout
  and and_19 (and_19_out, CU_P_en, ~CMD_CONST_10[4], ~CMD_CONST_10[5], CMD_CONST_10[6], ~CMD_CONST_10[7]);  // AND_Gate
  Subtractor #(.width(4)) subtractor_2 (.a(adder_5_out), .b(4'b0001), .out(Player_Tile));  // open: bin, bout
  assign IDB = and_19_out ? {{12{1'b0}}, multiplexer_28_out} : 16'bz;  // Controlled_Buffer controlled_buffer_13
  Multiplexer #(.select(4), .width(16)) multiplexer_29 (
    .in0(OUT_0), .in1(OUT_1), .in2(OUT_2), .in3(OUT_3), .in4(OUT_4), .in5(OUT_5), .in6(OUT_6_t), .in7(OUT_7),
    .in8(OUT_8), .in9(OUT_9), .in10(OUT_10), .in11(OUT_11), .in12(OUT_12), .in13(OUT_13), .in14(OUT_14),
    .in15(OUT_15), .out(TILE_STATUS), .sel(Player_Tile));
  Hex_Digit_Display hex_digit_display_15 (.value(Player_Tile));  // open: dp
  Multiplexer #(.select(4), .width(16)) multiplexer_30 (
    .in0(OUT_0), .in1(OUT_1), .in2(OUT_2), .in3(OUT_3), .in4(OUT_4), .in5(OUT_5), .in6(OUT_6_t), .in7(OUT_7),
    .in8(OUT_8), .in9(OUT_9), .in10(OUT_10), .in11(OUT_11), .in12(OUT_12), .in13(OUT_13), .in14(OUT_14),
    .in15(OUT_15), .sel(Player_Tile));  // open: out

  // Other names for the same wires on the sheet: CU_REG_SELECT[1:0] = CMD_CONST_10[9:8];
  //   REG_DESTINATION[2:0] = CMD_CONST_10[8:6]; CMDConst8[7:0] = CMD_CONST_10[7:0]; PAB[7:0] = CMD_CONST_10[7:0];
  //   REG_SOURCE_2[2:0] = CMD_CONST_10[2:0]; REG_SOURCE_1[2:0] = CMD_CONST_10[5:3]; px_x[5:0] = off_x;
  //   px_y[5:0] = off_y; tile_x[1:0] = px_x; tile_y[1:0] = px_y; ALU_SHIFT[3:0] = ALU_B[3:0]; ALU_B_SIGN = ALU_B[15];
  //   PPU_CLK = clk; IDB_SIGN = IDB[15]; JOY_X[1:0] = PLAYER_JOYSTICK

  // Notes on the sheet:
  //   Debug_ON: initial=0x1
  //   Prescaler anpassen wenn PC langsam
  //   SPLASH_IMPORTED_FROM_B2
  //   Der Mikrocode setzt eine interne Codierung von Bitsignalen speziell für die einzelnen Instruktionen.
  //   Langer Befehl
  //   3,3,10
  //   contents of uP_memory (hex, n*v repeats v):
  //   0 0 0 40 252*0 a02040 0 800000 a02000 4*0 c04040 0 800000 c04000 6*0 884400 80b040 6*0 884600 80b040
  //   6*0 884800 80b040 6*0 884a00 80b040 6*0 884c00 80b040 6*0 884e00 80b040 326*0 1 41 14*0 8 48 14*0 2
  //   42 14*0 10 50 14*0 4 44 14*0 20 60 15*0 100040 28*0 40 0 14000 b000 28*0 b040 0 4200 9b200 30*0
  //   40000 4a040 30*0 44000 40 29*0 a080 a080 40 30*0 4000 a1c0 30*0 14000 21040 32447*0 100040 15*0
  //   100040 15*0 100040 15*0 100040 15*0 100040 15*0 100040 32043*0 ffffffff
  //   address bus instructions
  //   Scoreboard
  //   Koordinaten neues Rechteck
  //   Koordinaten altes Rechteck
  //   linke Kante
  //   obere Kante
  //   rechte Kante
  //   untere Kante
  //   Hintergrundfarbe zum Löschen
  //   contents of instruction_memory (hex, n*v repeats v):
  //   0 0 e000 e101 e202 e303 e404 e500 da00 db01 da02 db03 db04 da05 db06 da07 d808 d809 dc0a d80b d80c
  //   d90d d80e d80f d406 f517
  //   inc_PC
  //   1
  //   Positionszähler
  //   Ablaufsteuerung
  //   CU_Register_read_write
  //   aktuelle Spalte
  //   aktuelle Zeile
  //   1
  //   bei normalen Blit immer 1 beide
  //   Register Write Enable
  //   X zurücksetzen
  //   X übernehmen
  //   Endbedingungen
  //   Steuersignale
  //   Y zurücksetzen
  //   Y übernehmen
  //   1000
  //   Internal Data Bus
  //   Reg0
  //   Reg1
  //   MAR
  //   Reg2
  //   MDR
  //   Reg3
  //   Reg4
  //   Reg5
  //   Reg6
  //   Reg7
  //   100
  //   Accumulator
  //   Memory Address Register
  //   Memory Data Register
  //   Register Read Select
  //   ALU
  //   SignHandling
  //   Overflow
  //   Carry
  //   DIV_0_compare
  //   ALU Operations
  //   MUX for RD_to_IDB
  //   contents of SPRITE_MEMORY (hex, n*v repeats v):
  //   5726*0 4*3 60*0 4*3 60*0 4*3 60*0 4*3 60*0 4*3 60*0 4*3 60*0 4*3 60*0 4*3 60*0 4*3 54*0 16*3 48*0
  //   16*3 48*0 16*3 48*0 16*3 48*0 16*3 48*0 16*3 48*0 16*3 48*0 16*3 36*0 40*3 24*0 40*3 24*0 40*3 24*0
  //   40*3 24*0 40*3 24*0 40*3 24*0 40*3 24*0 40*3 24*0 40*3 18*0 52*3 12*0 52*3 12*0 52*3 12*0 52*3 12*0
  //   52*3 12*0 12*3 28*0 12*3 12*0 12*3 28*0 12*3 12*0 12*3 28*0 12*3 12*0 12*3 28*0 12*3 1044*0 6*1 24*0
  //   6*1 28*0 6*1 24*0 6*1 28*0 6*1 24*0 6*1 28*0 6*1 24*0 6*1 28*0 6*1 24*0 6*1 28*0 6*1 24*0 6*1 34*0
  //   24*1 40*0 24*1 40*0 24*1 40*0 24*1 40*0 24*1 40*0 24*1 32*0 40*1 24*0 40*1 24*0 40*1 24*0 40*1 24*0
  //   6*1 6*0 16*1 6*0 6*1 24*0 6*1 6*0 16*1 6*0 6*1 24*0 6*1 6*0 16*1 6*0 6*1 24*0 6*1 6*0 16*1 6*0 6*1
  //   24*0 6*1 6*0 16*1 6*0 6*1 24*0 6*1 6*0 16*1 6*0 6*1 24*0 40*1 24*0 40*1 24*0 40*1 24*0 40*1 24*0
  //   40*1 24*0 40*1 24*0 40*1 24*0 40*1 20*0 12*1 8*0 8*1 8*0 12*1 16*0 12*1 8*0 8*1 8*0 12*1 16*0 12*1
  //   8*0 8*1 8*0 12*1 16*0 12*1 8*0 8*1 8*0 12*1 16*0 12*1 8*0 8*1 8*0 12*1 16*0 12*1 8*0 8*1 8*0 12*1
  //   16*0 12*1 8*0 8*1 8*0 12*1 16*0 12*1 8*0 8*1 8*0 12*1 1680*0 8*2 32*0 8*2 16*0 8*2 32*0 8*2 16*0 8*2
  //   32*0 8*2 16*0 8*2 32*0 8*2 16*0 8*2 6*0 20*2 6*0 8*2 16*0 8*2 6*0 20*2 6*0 8*2 30*0 20*2 44*0 20*2
  //   44*0 20*2 44*0 20*2 44*0 20*2 44*0 20*2 32*0 44*2 20*0 44*2 20*0 44*2 20*0 44*2 20*0 10*2 6*0 12*2
  //   6*0 10*2 20*0 10*2 6*0 12*2 6*0 10*2 20*0 10*2 6*0 12*2 6*0 10*2 20*0 10*2 6*0 12*2 6*0 10*2 20*0
  //   10*2 6*0 12*2 6*0 10*2 20*0 10*2 6*0 12*2 6*0 10*2 14*0 56*2 8*0 56*2 8*0 56*2 8*0 56*2 8*0 56*2 8*0
  //   56*2 14*0 44*2 20*0 44*2 20*0 44*2 20*0 44*2 24*0 12*2 12*0 12*2 28*0 12*2 12*0 12*2 28*0 12*2 12*0
  //   12*2 28*0 12*2 12*0 12*2 28*0 12*2 12*0 12*2 28*0 12*2 12*0 12*2 28*0 12*2 12*0 12*2 28*0 12*2 12*0
  //   12*2 1324*0 4*3 60*0 4*3 60*0 4*3 60*0 4*3 60*0 4*3 60*0 4*3 56*0 12*3 52*0 12*3 52*0 12*3 52*0 12*3
  //   52*0 12*3 52*0 12*3 52*0 12*3 52*0 12*3 56*0 4*3 60*0 4*3 60*0 4*3 60*0 4*3 60*0 4*3 60*0 4*3 60*0
  //   4*3 60*0 4*3 60*0 4*3 60*0 4*3 60*0 4*3 60*0 4*3 60*0 4*3 60*0 4*3 60*0 4*3 60*0 4*3 60*0 4*3 60*0
  //   4*3 60*0 4*3 60*0 4*3 56*0 12*3 52*0 12*3 52*0 12*3 52*0 12*3 52*0 12*3 52*0 12*3 52*0 12*3 52*0
  //   12*3 56*0 4*3 60*0 4*3 60*0 4*3 60*0 4*3 60*0 4*3 60*0 4*3
  //   adresse im COLOR_TABLE
  //   contents of COLOR_TABLE (hex, n*v repeats v):
  //   0 7e0 f800 ffff
  //   MUX for RENDERING
  //   farben in 5-6-5 r-g-b
  //   MUX for TILE_STATUS
  //   MUX for TILE_STATUS
endmodule

module ALU_FLAG_STATUS (
  input  ALU_Zero_Flag,
  input  Bit0,
  input  ALU_CARRY_Flag,
  input  Bit1,
  input  ALU_Overflow_Flag,
  input  Bit2,
  input  Bit3,
  input  Bit4,
  input  Bit5,
  output out_10
);

  wire and_1_out, and_2_out, and_3_out, and_4_out, and_5_out, and_6_out;

  and and_1 (and_1_out, ALU_Zero_Flag, Bit0);
  and and_2 (and_2_out, ALU_CARRY_Flag, Bit1);
  and and_3 (and_3_out, ALU_Overflow_Flag, Bit2);
  and and_4 (and_4_out, ~ALU_Zero_Flag, Bit3);  // AND_Gate
  and and_5 (and_5_out, ~ALU_CARRY_Flag, Bit4);  // AND_Gate
  and and_6 (and_6_out, ~ALU_Overflow_Flag, Bit5);  // AND_Gate
  or or_1 (out_10, and_1_out, and_2_out, and_3_out, and_4_out, and_5_out, and_6_out);
endmodule
